// Logisim project Act_2.circ as structural Verilog: 5 circuits, main circuit main
module main (
  input  in_1,
  input  in_2,
  input  in_3,
  input  in_4
);

  wire comparador_2bits_1_igual, comparador_2bits_1_mayor, comparador_2bits_1_menor,
       decodificador_4bits_7seg_1_b, decodificador_4bits_7seg_1_c, leds_indicadores_1_led_a,
       leds_indicadores_1_led_b, leds_indicadores_1_led_comp, leds_indicadores_1_led_sum;

  sumador_2bits sumador_2bits_1 ();  // open: A1A0, B1B0, S2, S1, S0
  comparador_2bits comparador_2bits_1 (
    .A1(in_1), .A0(in_2), .B1(in_3), .B0(in_4), .Mayor(comparador_2bits_1_mayor),
    .Menor(comparador_2bits_1_menor), .Igual(comparador_2bits_1_igual));
  decodificador_4bits_7seg decodificador_4bits_7seg_1 (
    .D2(comparador_2bits_1_mayor), .D1(comparador_2bits_1_menor), .D0(comparador_2bits_1_igual),
    .b(decodificador_4bits_7seg_1_b), .c(decodificador_4bits_7seg_1_c));  // open: a, d, e, f, g
  _7_Segment_Display u_7_segment_display_1 (
    .g(decodificador_4bits_7seg_1_b), .f(decodificador_4bits_7seg_1_b), .a(decodificador_4bits_7seg_1_b),
    .e(decodificador_4bits_7seg_1_c), .d(decodificador_4bits_7seg_1_c));  // open: b, c, dp
  Multiplexer multiplexer_1 ();  // open: in0, in1, out, sel
  leds_indicadores leds_indicadores_1 (
    .LED_A(leds_indicadores_1_led_a), .LED_B(leds_indicadores_1_led_b), .LED_Sum(leds_indicadores_1_led_sum),
    .LED_Comp(leds_indicadores_1_led_comp));  // open: S1, S0
  LED led_1 (.in(leds_indicadores_1_led_b));
  LED led_2 (.in(leds_indicadores_1_led_sum));
  LED led_3 (.in(leds_indicadores_1_led_comp));
  LED led_4 (.in(leds_indicadores_1_led_a));
endmodule

module sumador_2bits (
  input  [1:0] A1A0,
  input  [1:0] B1B0,
  output S2,
  output S1,
  output S0
);

  wire nand_1_out, nand_2_out, nand_3_out, nand_4_out, nand_5_out, nand_6_out, nand_7_out, nand_8_out,
       nand_9_out, nand_10_out, nand_11_out, nand_12_out, nand_13_out, nand_14_out, nand_15_out, nand_16_out,
       nand_17_out, nand_18_out, nand_20_out, nand_21_out, nand_22_out, nand_23_out, nand_24_out,
       nand_25_out, nand_26_out, nand_27_out, nand_28_out, nand_29_out, nand_30_out, nand_31_out,
       nand_32_out, nand_33_out, nand_34_out, nand_35_out, nand_36_out, nand_37_out, nand_38_out,
       nand_39_out, nand_40_out, nand_41_out, nand_42_out, nand_44_out, nand_45_out, nand_46_out, nand_47_out;

  nand nand_1 (nand_1_out, 1'b1, A1A0[1]);
  nand nand_2 (nand_2_out, 1'b1, A1A0[0]);
  nand nand_3 (nand_3_out, 1'b1, B1B0[1]);
  nand nand_4 (nand_4_out, 1'b1, B1B0[0]);
  nand nand_5 (nand_5_out, A1A0[0], B1B0[1]);
  nand nand_6 (nand_6_out, nand_1_out, nand_2_out);
  nand nand_7 (nand_7_out, nand_1_out, A1A0[0]);
  nand nand_8 (nand_8_out, nand_3_out, B1B0[0]);
  nand nand_9 (nand_9_out, A1A0[1], nand_2_out);
  nand nand_10 (nand_10_out, A1A0[1], nand_3_out);
  nand nand_11 (nand_11_out, nand_2_out, B1B0[0]);
  nand nand_12 (nand_12_out, A1A0[0], nand_4_out);
  nand nand_13 (nand_13_out, nand_5_out, nand_5_out);
  nand nand_14 (nand_14_out, nand_6_out, nand_6_out);
  nand nand_15 (nand_15_out, nand_7_out, nand_7_out);
  nand nand_16 (nand_16_out, nand_8_out, nand_8_out);
  nand nand_17 (nand_17_out, nand_9_out, nand_9_out);
  nand nand_18 (nand_18_out, nand_10_out, nand_10_out);
  nand nand_19 (S0, nand_11_out, nand_12_out);
  nand nand_20 (nand_20_out, nand_13_out, B1B0[0]);
  nand nand_21 (nand_21_out, A1A0[1], B1B0[1]);
  nand nand_22 (nand_22_out, A1A0[1], A1A0[0]);
  nand nand_23 (nand_23_out, nand_14_out, B1B0[1]);
  nand nand_24 (nand_24_out, nand_15_out, nand_16_out);
  nand nand_25 (nand_25_out, nand_1_out, B1B0[1]);
  nand nand_26 (nand_26_out, nand_17_out, nand_3_out);
  nand nand_27 (nand_27_out, nand_18_out, nand_4_out);
  nand nand_28 (nand_28_out, A1A0[1], A1A0[0]);
  nand nand_29 (nand_29_out, B1B0[1], B1B0[0]);
  nand nand_30 (nand_30_out, nand_20_out, nand_21_out);
  nand nand_31 (nand_31_out, nand_22_out, nand_22_out);
  nand nand_32 (nand_32_out, nand_23_out, nand_24_out);
  nand nand_33 (nand_33_out, nand_25_out, nand_25_out);
  nand nand_34 (nand_34_out, nand_26_out, nand_27_out);
  nand nand_35 (nand_35_out, nand_28_out, nand_28_out);
  nand nand_36 (nand_36_out, nand_29_out, nand_29_out);
  nand nand_37 (nand_37_out, nand_30_out, nand_30_out);
  nand nand_38 (nand_38_out, nand_31_out, B1B0[0]);
  nand nand_39 (nand_39_out, nand_32_out, nand_32_out);
  nand nand_40 (nand_40_out, nand_33_out, nand_4_out);
  nand nand_41 (nand_41_out, nand_34_out, nand_34_out);
  nand nand_42 (nand_42_out, nand_35_out, nand_36_out);
  nand nand_43 (S2, nand_37_out, nand_38_out);
  nand nand_44 (nand_44_out, nand_39_out, nand_40_out);
  nand nand_45 (nand_45_out, nand_41_out, nand_42_out);
  nand nand_46 (nand_46_out, nand_44_out, nand_44_out);
  nand nand_47 (nand_47_out, nand_45_out, nand_45_out);
  nand nand_48 (S1, nand_46_out, nand_47_out);
endmodule

module comparador_2bits (
  input  A1,
  input  A0,
  input  B1,
  input  B0,
  output Mayor,
  output Menor,
  output Igual
);

  wire nand_1_out, nand_2_out, nand_3_out, nand_4_out, nand_5_out, nand_6_out, nand_7_out, nand_8_out,
       nand_9_out, nand_10_out, nand_11_out, nand_12_out, nand_13_out, nand_14_out, nand_15_out, nand_16_out,
       nand_17_out, nand_18_out, nand_19_out, nand_20_out, nand_21_out, nand_22_out, nand_23_out,
       nand_24_out, nand_25_out, nand_26_out, nand_27_out, nand_28_out, nand_29_out, nand_30_out,
       nand_31_out, nand_32_out, nand_33_out, nand_34_out, nand_35_out, nand_36_out, nand_37_out,
       nand_38_out, nand_39_out, nand_40_out, nand_41_out, nand_42_out, nand_43_out, nand_44_out,
       nand_45_out, nand_46_out;

  nand nand_1 (nand_1_out, 1'b1, A1);
  nand nand_2 (nand_2_out, 1'b1, A0);
  nand nand_3 (nand_3_out, 1'b1, B1);
  nand nand_4 (nand_4_out, 1'b1, B0);
  nand nand_5 (nand_5_out, A0, nand_3_out);
  nand nand_6 (nand_6_out, nand_1_out, nand_2_out);
  nand nand_7 (nand_7_out, nand_1_out, nand_2_out);
  nand nand_8 (nand_8_out, nand_3_out, nand_4_out);
  nand nand_9 (nand_9_out, nand_1_out, A0);
  nand nand_10 (nand_10_out, nand_3_out, B0);
  nand nand_11 (nand_11_out, A1, nand_2_out);
  nand nand_12 (nand_12_out, B1, nand_4_out);
  nand nand_13 (nand_13_out, A1, A0);
  nand nand_14 (nand_14_out, B1, B0);
  nand nand_15 (nand_15_out, nand_5_out, nand_5_out);
  nand nand_16 (nand_16_out, nand_6_out, nand_6_out);
  nand nand_17 (nand_17_out, nand_7_out, nand_7_out);
  nand nand_18 (nand_18_out, nand_8_out, nand_8_out);
  nand nand_19 (nand_19_out, nand_9_out, nand_9_out);
  nand nand_20 (nand_20_out, nand_10_out, nand_10_out);
  nand nand_21 (nand_21_out, nand_11_out, nand_11_out);
  nand nand_22 (nand_22_out, nand_12_out, nand_12_out);
  nand nand_23 (nand_23_out, nand_13_out, nand_13_out);
  nand nand_24 (nand_24_out, nand_14_out, nand_14_out);
  nand nand_25 (nand_25_out, nand_15_out, nand_4_out);
  nand nand_26 (nand_26_out, A1, nand_3_out);
  nand nand_27 (nand_27_out, A1, A0);
  nand nand_28 (nand_28_out, nand_16_out, B0);
  nand nand_29 (nand_29_out, nand_1_out, B1);
  nand nand_30 (nand_30_out, nand_2_out, B1);
  nand nand_31 (nand_31_out, nand_17_out, nand_18_out);
  nand nand_32 (nand_32_out, nand_19_out, nand_20_out);
  nand nand_33 (nand_33_out, nand_21_out, nand_22_out);
  nand nand_34 (nand_34_out, nand_23_out, nand_24_out);
  nand nand_35 (nand_35_out, nand_25_out, nand_26_out);
  nand nand_36 (nand_36_out, nand_27_out, nand_27_out);
  nand nand_37 (nand_37_out, nand_28_out, nand_29_out);
  nand nand_38 (nand_38_out, nand_30_out, nand_30_out);
  nand nand_39 (nand_39_out, nand_31_out, nand_32_out);
  nand nand_40 (nand_40_out, nand_33_out, nand_34_out);
  nand nand_41 (nand_41_out, nand_35_out, nand_35_out);
  nand nand_42 (nand_42_out, nand_36_out, nand_4_out);
  nand nand_43 (nand_43_out, nand_37_out, nand_37_out);
  nand nand_44 (nand_44_out, nand_38_out, B0);
  nand nand_45 (nand_45_out, nand_39_out, nand_39_out);
  nand nand_46 (nand_46_out, nand_40_out, nand_40_out);
  nand nand_47 (Mayor, nand_41_out, nand_42_out);
  nand nand_48 (Menor, nand_43_out, nand_44_out);
  nand nand_49 (Igual, nand_45_out, nand_46_out);
endmodule

module decodificador_4bits_7seg (
  input  D2,
  input  D1,
  input  D0,
  output a,
  output b,
  output c,
  output d,
  output e,
  output f,
  output g
);

  wire and_1_out, and_2_out, and_3_out, and_4_out, and_5_out, and_6_out, and_7_out, and_8_out, and_9_out,
       and_10_out, and_11_out, and_12_out, and_13_out, and_14_out, and_15_out, and_16_out, not_1_out,
       not_2_out, not_3_out;

  not not_1 (not_1_out, D2);
  not not_2 (not_2_out, D1);
  not not_3 (not_3_out, D0);
  and and_1 (and_1_out, not_1_out, not_3_out);
  and and_2 (and_2_out, D2, D0);
  and and_3 (and_3_out, not_2_out, not_3_out);
  and and_4 (and_4_out, D1, D0);
  or or_1 (c, not_2_out, D0, D2);
  and and_5 (and_5_out, not_1_out, not_3_out);
  and and_6 (and_6_out, not_1_out, D1);
  and and_7 (and_7_out, D2, not_2_out, D0);
  and and_8 (and_8_out, D1, not_3_out);
  and and_9 (and_9_out, not_1_out, not_3_out);
  and and_10 (and_10_out, D1, not_3_out);
  and and_11 (and_11_out, not_2_out, not_3_out);
  and and_12 (and_12_out, D2, not_2_out);
  and and_13 (and_13_out, D2, not_3_out);
  and and_14 (and_14_out, not_1_out, D1);
  and and_15 (and_15_out, D2, not_2_out);
  and and_16 (and_16_out, D1, not_3_out);
  or or_2 (a, and_1_out, D1, and_2_out);
  or or_3 (b, not_1_out, and_3_out, and_4_out);
  or or_4 (d, and_5_out, and_6_out, and_7_out, and_8_out);
  or or_5 (e, and_9_out, and_10_out);
  or or_6 (f, and_11_out, and_12_out, and_13_out);
  or or_7 (g, and_14_out, and_15_out, and_16_out);
endmodule

module leds_indicadores (
  input  S1,
  input  S0,
  output LED_A,
  output LED_B,
  output LED_Sum,
  output LED_Comp
);

  wire nand_1_out, nand_2_out, nand_3_out, nand_4_out, nand_5_out, nand_6_out;

  nand nand_1 (nand_1_out, 1'b1, S1);
  nand nand_2 (nand_2_out, 1'b1, S0);
  nand nand_3 (nand_3_out, nand_1_out, nand_2_out);
  nand nand_4 (nand_4_out, nand_1_out, S0);
  nand nand_5 (nand_5_out, S1, nand_2_out);
  nand nand_6 (nand_6_out, S1, S0);
  nand nand_7 (LED_A, nand_3_out, nand_3_out);
  nand nand_8 (LED_B, nand_4_out, nand_4_out);
  nand nand_9 (LED_Sum, nand_5_out, nand_5_out);
  nand nand_10 (LED_Comp, nand_6_out, nand_6_out);
endmodule
